// Digital circuit PC_tb.dig as structural Verilog
module PC_tb (
  input  clock,
  input  reset,
  input  wen,
  output [31:0] address
);

  wire [31:0] pc_1_p1;

  // PC pc_1: pin names not known; wires that end beside it: pc_1_p1, wen, reset, clock, address
  Add #(.Bits(32)) add_1 (.a(32'h4), .b(address), .c_i(1'b0), .s(pc_1_p1));  // open: c_o
endmodule
