// Digital circuit program-mem.dig as structural Verilog
module program_mem (
  input  [31:0] addr,
  output [31:0] instr
);

  wire [23:0] add_1_s, add_2_s, add_3_s;

  Add #(.Bits(24)) add_1 (.a(addr[23:0]), .b(24'h1), .c_i(1'b0), .s(add_1_s));  // open: c_o
  ROM #(.AddrBits(24), .Bits(8)) rom_1 (.A(addr[23:0]), .sel(1'b1), .D(instr[31:24]));
  Add #(.Bits(24)) add_2 (.a(add_1_s), .b(24'h1), .c_i(1'b0), .s(add_2_s));  // open: c_o
  ROM #(.AddrBits(24), .Bits(8)) rom_2 (.A(add_1_s), .sel(1'b1), .D(instr[23:16]));
  Add #(.Bits(24)) add_3 (.a(add_2_s), .b(24'h1), .c_i(1'b0), .s(add_3_s));  // open: c_o
  ROM #(.AddrBits(24), .Bits(8)) rom_3 (.A(add_2_s), .sel(1'b1), .D(instr[15:8]));
  ROM #(.AddrBits(24), .Bits(8)) rom_4 (.A(add_3_s), .sel(1'b1), .D(instr[7:0]));

  // Notes on the sheet:
  //   contents of rom_1 (hex, n*v repeats v):
  //   fe,1,1,13,0,11,2e,23,0,81,2c,23,2,1,4,13,0,0,5,13,fe,a4,2a,23
  //   ,fe,a4,28,23,1,30,5,93,fe,b4,26,23,2,a0,5,93,fe,b4,24,23,fe,c4
  //   ,25,83,fe,84,26,3,0,c5,85,b3,fe,b4,28,23,1,c1,20,83,1,81,24,3
  //   ,2,1,1,13,0,a0,8,93,0,0,0,73
  //   contents of rom_2 (hex, n*v repeats v):
  //   fe,1,1,13,0,11,2e,23,0,81,2c,23,2,1,4,13,0,0,5,13,fe,a4,2a,23
  //   ,fe,a4,28,23,1,30,5,93,fe,b4,26,23,2,a0,5,93,fe,b4,24,23,fe,c4
  //   ,25,83,fe,84,26,3,0,c5,85,b3,fe,b4,28,23,1,c1,20,83,1,81,24,3
  //   ,2,1,1,13,0,a0,8,93,0,0,0,73
  //   contents of rom_3 (hex, n*v repeats v):
  //   fe,1,1,13,0,11,2e,23,0,81,2c,23,2,1,4,13,0,0,5,13,fe,a4,2a,23
  //   ,fe,a4,28,23,1,30,5,93,fe,b4,26,23,2,a0,5,93,fe,b4,24,23,fe,c4
  //   ,25,83,fe,84,26,3,0,c5,85,b3,fe,b4,28,23,1,c1,20,83,1,81,24,3
  //   ,2,1,1,13,0,a0,8,93,0,0,0,73
  //   contents of rom_4 (hex, n*v repeats v):
  //   fe,1,1,13,0,11,2e,23,0,81,2c,23,2,1,4,13,0,0,5,13,fe,a4,2a,23
  //   ,fe,a4,28,23,1,30,5,93,fe,b4,26,23,2,a0,5,93,fe,b4,24,23,fe,c4
  //   ,25,83,fe,84,26,3,0,c5,85,b3,fe,b4,28,23,1,c1,20,83,1,81,24,3
  //   ,2,1,1,13,0,a0,8,93,0,0,0,73
endmodule
