// Digital circuit control_unit.dig as structural Verilog
module control_unit (
  input  [31:0] inst,
  output imm_reg,
  output dmwen,
  output [1:0] WBsel,
  output Store,
  output Branch,
  output [2:0] Funct3,
  output Srai_sub,
  output [6:0] Funct7,
  output JAL_JARL,
  output Load,
  output [6:0] Opcode,
  output rfwen
);

  wire Imm_eq, JAL_eq, JALR_eq, Load_eq, or_3_out, R_eq;
  wire [1:0] multiplexer_2_out;
  wire [2:0] splitter_1_funct3;

  splitter splitter_1 (
    .inst(inst), .opcode(Opcode), .funct3(splitter_1_funct3), .funct7(Funct7));  // open: rd, rs1, rs2
  Comparator #(.Signed("true"), .Bits(7)) R (.a(Opcode), .b(7'b0110011), .eq(R_eq));  // open: gt, lt
  Comparator #(.Signed("true"), .Bits(7)) Imm (.a(Opcode), .b(7'b0010011), .eq(Imm_eq));  // open: gt, lt
  Comparator #(.Signed("true"), .Bits(7)) S (.a(Opcode), .b(7'b0001001), .eq(dmwen));  // open: gt, lt
  Comparator #(.Signed("true"), .Bits(7)) u_Load (.a(Opcode), .b(7'b0000011), .eq(Load_eq));  // open: gt, lt
  Comparator #(.Signed("true"), .Bits(7)) JAL (.a(Opcode), .b(7'b1101111), .eq(JAL_eq));  // open: gt, lt
  Comparator #(.Signed("true"), .Bits(7)) JALR (.a(Opcode), .b(7'b1100111), .eq(JALR_eq));  // open: gt, lt
  Comparator #(.Signed("true"), .Bits(7)) u_Store (.a(Opcode), .b(7'b0100011), .eq(Store));  // open: gt, lt
  Comparator #(.Signed("true"), .Bits(7)) Load_2 (.a(Opcode), .b(7'b0000011), .eq(Load));  // open: gt, lt
  Comparator #(.Signed("true"), .Bits(7)) u_Branch (.a(Opcode), .b(7'b1100011), .eq(Branch));  // open: gt, lt
  not not_1 (imm_reg, R_eq);
  or or_1 (rfwen, R_eq, JALR_eq, Imm_eq, Load);
  or or_2 (JAL_JARL, JAL_eq, JALR_eq);
  Multiplexer #(.Bits(3)) multiplexer_1 (.sel(Branch), .in_0(splitter_1_funct3), .in_1(3'b000), .out(Funct3));
  Multiplexer #(.Bits(2)) multiplexer_2 (.sel(JAL_JARL), .in_0(2'b00), .in_1(2'b10), .out(multiplexer_2_out));
  or or_3 (or_3_out, Branch, dmwen, Imm_eq);
  Multiplexer #(.Bits(2)) multiplexer_3 (.sel(Load_eq), .in_0(multiplexer_2_out), .in_1(2'b01), .out(WBsel));
  Multiplexer multiplexer_4 (.sel(or_3_out), .in_0(Funct7[1]), .in_1(1'b0), .out(Srai_sub));
endmodule
