// Digital circuit pc.dig as structural Verilog
module pc (
  input  clock,
  input  reset,
  input  wen,
  output [31:0] address
);

  wire [31:0] add_1_s;

  pc_stage pc_stage_1 (.\input (add_1_s), .wen(wen), .reset(reset), .clock(clock), .\output (address));
  Add #(.Bits(32)) add_1 (.a(32'h4), .b(address), .c_i(1'b0), .s(add_1_s));  // open: c_o
endmodule
