// Digital circuit pc_stage.dig as structural Verilog
module pc_stage (
  input  [31:0] \input ,
  input  wen,
  input  reset,
  input  clock,
  output [31:0] \output 
);

  wire or_1_out;
  wire [31:0] multiplexer_1_out, multiplexer_2_out;

  Multiplexer #(.Bits(32)) multiplexer_1 (.sel(wen), .in_0(\output ), .in_1(\input ), .out(multiplexer_1_out));
  Multiplexer #(.Bits(32)) multiplexer_2 (
    .sel(reset), .in_0(multiplexer_1_out), .in_1({32{1'b0}}), .out(multiplexer_2_out));
  or or_1 (or_1_out, wen, reset);
  Register #(.Bits(32)) PC (.D(multiplexer_2_out), .C(clock), .en(or_1_out), .Q(\output ));
endmodule
